# Fritzing sketch rfid-rc522_with_leds_PJyl6FiRbc (saved by Fritzing 0.9.3b)
breadboards: 1

parts:
  Parte1 = Arduino Uno (Rev3)
  RFID-RC522 = RFID USB Reader
  LED1 = LED - 5mm [color="Red (633nm)" package="5 mm [THT]"]
  LED2 = LED - 5mm [color="Green (560nm)" package="5 mm [THT]"]
  R1 = Resistor [tolerance=±5% resistance=220 package=THT]
  R2 = Resistor [tolerance=±5% resistance=220 package=THT]

nets:
  N1: Parte1.A0, R1.Pin_1
  N2: Parte1.A1, R2.Pin_1
  N3: Parte1.D9_PWM, RFID-RC522.GND
  N4: Parte1.D10_PWM/SS, RFID-RC522.GNDT
  N5: Parte1.D11_PWM/MOSI, RFID-RC522.ANT2
  N6: Parte1.D12/MISO, RFID-RC522.ANT1
  N7: Parte1.D13/SCK, RFID-RC522.CP
  3V3: Parte1.3V3, RFID-RC522.VCC
  N8: Parte1.GND, RFID-RC522.TX-O, LED1.cathode, LED2.cathode
  N9: LED1.anode, R1.Pin_0
  N10: LED2.anode, R2.Pin_0
